# Fritzing sketch 01_PULSE (saved by Fritzing 0.9.3b)
breadboards: 1

parts:
  Part1 = Adafruit Metro Mini [part_number="Adafruit #2590"]
  R1 = Resistor [tolerance=±5% resistance=220 package=THT]
  R2 = Resistor [tolerance=±5% resistance=220 package=THT]
  R3 = Resistor [tolerance=±5% resistance=220 package=THT]
  R4 = Resistor [tolerance=±5% resistance=220 package=THT]
  R5 = Resistor [tolerance=±5% resistance=220 package=THT]
  R6 = Resistor [tolerance=±5% resistance=100k package=THT]
  R7 = Resistor [tolerance=±5% resistance=220 package=THT]
  R8 = Resistor [tolerance=±5% resistance=220 package=THT]
  R9 = Resistor [tolerance=±5% resistance=220 package=THT]
  R10 = Resistor [tolerance=±5% resistance=220 package=THT]
  R11 = Resistor [tolerance=±5% resistance=220 package=THT]
  R12 = Resistor [tolerance=±5% resistance=220 package=THT]
  R13 = Resistor [tolerance=±5% resistance=220 package=THT]
  R14 = Resistor [tolerance=±5% resistance=220 package=THT]
  R15 = Resistor [tolerance=±5% resistance=220 package=THT]
  R16 = Resistor [tolerance=±5% resistance=220 package=THT]
  R17 = Resistor [tolerance=±5% resistance=220 package=THT]
  R18 = Resistor [tolerance=±5% resistance=220 package=THT]
  R19 = Resistor [tolerance=±5% resistance=220 package=THT]
  R20 = Resistor [tolerance=±5% resistance=220 package=THT]
  R21 = Resistor [tolerance=±5% resistance=220 package=THT]
  R22 = Resistor [tolerance=±5% resistance=220 package=THT]
  U1 = 74HC595 [package="DIP16 [THT]"]
  U2 = 74HC595 [package="DIP16 [THT]"]
  J1_(Seq_A_Pulse_OUTPUT) = BANANA_CONN [package=banana_conn]
  S1_(Page_Switch_INPUT) = Round Pushbutton
  LED1 = LED - 5mm [color="Green (570nm)" package="5 mm [THT]"]
  J2_(Seq_B_Pulse_OUTPUT) = BANANA_CONN [package=banana_conn]
  LED2 = LED - 5mm [color="Yellow (595nm)" package="5 mm [THT]"]
  J3_(Seq_C_Pulse_OUTPUT) = BANANA_CONN [package=banana_conn]
  J4_(Seq_D_Pulse_OUTPUT) = BANANA_CONN [package=banana_conn]
  LED3 = LED - 5mm [color="Green (570nm)" package="5 mm [THT]"]
  LED4 = LED - 5mm [color="Yellow (595nm)" package="5 mm [THT]"]
  J5_(Ext_Pulse_INPUT) = BANANA_CONN [package=banana_conn]
  S2_(Up_Switch_INPUT) = Round Pushbutton
  S3_(Down_Switch_INPUT) = Round Pushbutton
  S4_(Select_Switch_INPUT) = Round Pushbutton
  LED5 = LED - 5mm [color="Red (633nm)" package="5 mm [THT]"]
  LED6 = LED - 5mm [color="Green (570nm)" package="5 mm [THT]"]
  LED7 = LED - 5mm [color="Yellow (592nm)" package="5 mm [THT]"]
  LED8 = LED - 5mm [color="Blue (525nm)" package="5 mm [THT]"]
  LED9 = LED - 5mm [color="Red (633nm)" package="5 mm [THT]"]
  LED10 = LED - 5mm [color="Green (570nm)" package="5 mm [THT]"]
  LED11 = LED - 5mm [color="Orange (620nm)" package="5 mm [THT]"]
  LED12 = LED - 5mm [color="Blue (525nm)" package="5 mm [THT]"]
  LED13 = LED - 5mm [color="Red (633nm)" package="5 mm [THT]"]
  LED14 = LED - 5mm [color="Green (570nm)" package="5 mm [THT]"]
  LED15 = LED - 5mm [color="Yellow (595nm)" package="5 mm [THT]"]
  LED16 = LED - 5mm [color="Blue (525nm)" package="5 mm [THT]"]
  LED17 = LED - 5mm [color="Red (633nm)" package="5 mm [THT]"]
  LED18 = LED - 5mm [color="Green (570nm)" package="5 mm [THT]"]
  LED19 = LED - 5mm [color="Orange (620nm)" package="5 mm [THT]"]
  LED20 = LED - 5mm [color="Blue (525nm)" package="5 mm [THT]"]
  GND = BANANA_CONN [package=banana_conn]
  +5V = BANANA_CONN [package=banana_conn]

nets:
  N1: Part1.AD0, R5.Pin_0, R6.Pin_1
  N2: Part1.IO13, U1.SH_CP, U2.SH_CP
  N3: Part1.IO12, U1.ST_CP, U2.ST_CP
  N4: Part1.IO11, U1.DS
  N5: Part1.IO10, R4.Pin_0
  N6: Part1.IO9, R3.Pin_0
  N7: Part1.IO8, R2.Pin_0
  N8: Part1.IO7, R1.Pin_0
  N9: Part1.IO5, S4_(Select_Switch_INPUT).leg0
  N10: Part1.IO4, S3_(Down_Switch_INPUT).leg0
  N11: Part1.IO3, S2_(Up_Switch_INPUT).leg0
  N12: Part1.IO2, S1_(Page_Switch_INPUT).leg0
  VCC: Part1.+5V, U1.MR, U1.VCC, U2.MR, U2.VCC
  GND: Part1.GND, R6.Pin_0, U1.GND, U1.OE, U2.GND, U2.Q7', U2.OE, S1_(Page_Switch_INPUT).leg1, LED1.cathode, LED2.cathode, LED3.cathode, LED4.cathode, S2_(Up_Switch_INPUT).leg1, S3_(Down_Switch_INPUT).leg1, S4_(Select_Switch_INPUT).leg1, LED5.cathode, LED6.cathode, LED7.cathode, LED8.cathode, LED9.cathode, LED10.cathode, LED11.cathode, LED12.cathode, LED13.cathode, LED14.cathode, LED15.cathode, LED16.cathode, LED17.cathode, LED18.cathode, LED19.cathode, LED20.cathode, GND.1
  N13: Part1.VIN, +5V.1
  N14: R1.Pin_1, J1_(Seq_A_Pulse_OUTPUT).1, LED1.anode
  N15: R2.Pin_1, J2_(Seq_B_Pulse_OUTPUT).1, LED2.anode
  N16: R3.Pin_1, J3_(Seq_C_Pulse_OUTPUT).1, LED3.anode
  N17: R4.Pin_1, J4_(Seq_D_Pulse_OUTPUT).1, LED4.anode
  N18: R5.Pin_1, J5_(Ext_Pulse_INPUT).1
  N19: R7.Pin_0, LED5.anode
  N20: R7.Pin_1, U1.Q0
  N21: R8.Pin_0, LED6.anode
  N22: R8.Pin_1, U1.Q1
  N23: R9.Pin_0, LED7.anode
  N24: R9.Pin_1, U1.Q2
  N25: R10.Pin_0, LED8.anode
  N26: R10.Pin_1, U1.Q3
  N27: R11.Pin_0, LED9.anode
  N28: R11.Pin_1, U1.Q4
  N29: R12.Pin_0, LED10.anode
  N30: R12.Pin_1, U1.Q5
  N31: R13.Pin_0, LED11.anode
  N32: R13.Pin_1, U1.Q6
  N33: R14.Pin_0, LED12.anode
  N34: R14.Pin_1, U1.Q7
  N35: R15.Pin_0, LED13.anode
  N36: R15.Pin_1, U2.Q0
  N37: R16.Pin_0, LED14.anode
  N38: R16.Pin_1, U2.Q1
  N39: R17.Pin_0, LED15.anode
  N40: R17.Pin_1, U2.Q2
  N41: R18.Pin_0, LED16.anode
  N42: R18.Pin_1, U2.Q3
  N43: R19.Pin_0, LED17.anode
  N44: R19.Pin_1, U2.Q4
  N45: R20.Pin_0, LED18.anode
  N46: R20.Pin_1, U2.Q5
  N47: R21.Pin_0, LED19.anode
  N48: R21.Pin_1, U2.Q6
  N49: R22.Pin_0, LED20.anode
  N50: R22.Pin_1, U2.Q7
  N51: U1.Q7', U2.DS

notes:
  01 PULSE, Shelfisizer Module #1: 4-Channel Sequencer - rld, 0.1b

custom parts:
  Adafruit Metro Mini: We sure love the ATmega328 here at Adafruit, and we use them a lot for our own projects. The processor has plenty of GPIO, Analog inputs, hardware UART SPI and I2C, timers and PWM galore - just enough for most simple projects. When we need to go small, we use a Pro Trinket 3V or 5V, but if you want to have USB-to-Serial built in, we reach for an Adafruit METRO Mini. METRO Mini is the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
