# Fritzing sketch 02_ONEBANG (saved by Fritzing 0.9.3b)
breadboards: 1

parts:
  Part1 = Adafruit Metro Mini [part_number="Adafruit #2590"]
  GND = BANANA_CONN [package=banana_conn]
  +5V = BANANA_CONN [package=banana_conn]
  R1 = Resistor [tolerance=±5% resistance=100k package=THT]
  J1_(Ext_Pulse_INPUT) = BANANA_CONN [package=banana_conn]
  R2 = Resistor [tolerance=±5% resistance=220 package=THT]
  R3 = Resistor [tolerance=±5% resistance=1k package=THT]
  R4 = Resistor [tolerance=±5% resistance=220 package=THT]
  R5 = Resistor [tolerance=±5% resistance=220 package=THT]
  R6 = Resistor [tolerance=±5% resistance=220 package=THT]
  R7 = Resistor [tolerance=±5% resistance=220 package=THT]
  R8 = Resistor [tolerance=±5% resistance=220 package=THT]
  R9 = Resistor [tolerance=±5% resistance=220 package=THT]
  R11 = Resistor [tolerance=±5% resistance=100k package=THT]
  R12 = Resistor [tolerance=±5% resistance=100k package=THT]
  R10 = Resistor [tolerance=±5% resistance=100k package=THT]
  R13 = Resistor [tolerance=±5% resistance=100k package=THT]
  R14 = Resistor [tolerance=±5% resistance=100k package=THT]
  R15 = Resistor [tolerance=±5% resistance=100k package=THT]
  J2_(CV_A_INPUT) = BANANA_CONN [package=banana_conn]
  J3_(CV_B_INPUT) = BANANA_CONN [package=banana_conn]
  J4_(CV_C_INPUT) = BANANA_CONN [package=banana_conn]
  J5_(CV_D_INPUT) = BANANA_CONN [package=banana_conn]
  J6_(CV_E_INPUT) = BANANA_CONN [package=banana_conn]
  J7_(CV_F_INPUT) = BANANA_CONN [package=banana_conn]
  J8_(TRIG_A_OUTPUT) = BANANA_CONN [package=banana_conn]
  S1_(Mode_Switch_INPUT) = Round Pushbutton
  LED1 = LED - 5mm [color="Yellow (595nm)" package="5 mm [THT]"]
  LED2 = LED - 5mm [color="Green (570nm)" package="5 mm [THT]"]
  J9_(TRIG_B_OUTPUT) = BANANA_CONN [package=banana_conn]
  J10_(TRIG_C_OUTPUT) = BANANA_CONN [package=banana_conn]
  J11_(TRIG_D_OUTPUT) = BANANA_CONN [package=banana_conn]
  J12_(TRIG_E_OUTPUT) = BANANA_CONN [package=banana_conn]
  J13_(TRIG_F_OUTPUT) = BANANA_CONN [package=banana_conn]
  LED3 = LED - 5mm [color="Blue (525nm)" package="5 mm [THT]"]
  LED4 = LED - 5mm [color="Blue (525nm)" package="5 mm [THT]"]
  LED5 = LED - 5mm [color="Blue (525nm)" package="5 mm [THT]"]
  LED6 = LED - 5mm [color="Blue (525nm)" package="5 mm [THT]"]
  LED7 = LED - 5mm [color="Blue (525nm)" package="5 mm [THT]"]
  LED8 = LED - 5mm [color="Blue (525nm)" package="5 mm [THT]"]
  LED9 = LED - 5mm [color="Red (633nm)" package="5 mm [THT]"]
  LED10 = LED - 5mm [color="Red (633nm)" package="5 mm [THT]"]
  LED12 = LED - 5mm [color="Red (633nm)" package="5 mm [THT]"]
  LED13 = LED - 5mm [color="Red (633nm)" package="5 mm [THT]"]
  LED14 = LED - 5mm [color="Red (633nm)" package="5 mm [THT]"]
  LED11 = LED - 5mm [color="Red (633nm)" package="5 mm [THT]"]

nets:
  N1: Part1.AD5/SCL, R15.Pin_1, J7_(CV_F_INPUT).1, LED8.anode
  N2: Part1.AD4/SDA, R14.Pin_1, J6_(CV_E_INPUT).1, LED7.anode
  N3: Part1.AD3, R13.Pin_1, J5_(CV_D_INPUT).1, LED6.anode
  N4: Part1.AD2, R12.Pin_1, J4_(CV_C_INPUT).1, LED5.anode
  N5: Part1.AD1, R11.Pin_1, J3_(CV_B_INPUT).1, LED4.anode
  N6: Part1.AD0, R10.Pin_1, J2_(CV_A_INPUT).1, LED3.anode
  N7: Part1.IO11, LED2.anode
  N8: Part1.IO10, LED1.anode
  N9: Part1.IO9, S1_(Mode_Switch_INPUT).leg0
  N10: Part1.IO8, R9.Pin_0
  N11: Part1.IO7, R8.Pin_0
  N12: Part1.IO6, R7.Pin_0
  N13: Part1.IO5, R6.Pin_0
  N14: Part1.IO4, R5.Pin_0
  N15: Part1.IO3, R4.Pin_0
  N16: Part1.IO2, R1.Pin_1, J1_(Ext_Pulse_INPUT).1
  N17: Part1.GND, GND.1, R1.Pin_0, R2.Pin_0, R3.Pin_0, R11.Pin_0, R12.Pin_0, R10.Pin_0, R13.Pin_0, R14.Pin_0, R15.Pin_0, S1_(Mode_Switch_INPUT).leg1
  N18: Part1.VIN, +5V.1
  N19: R2.Pin_1, LED1.cathode, LED2.cathode, LED3.cathode, LED4.cathode, LED5.cathode, LED6.cathode, LED7.cathode, LED8.cathode
  N20: R3.Pin_1, LED9.cathode, LED10.cathode, LED12.cathode, LED13.cathode, LED14.cathode, LED11.cathode
  N21: R4.Pin_1, J8_(TRIG_A_OUTPUT).1, LED9.anode
  N22: R5.Pin_1, J9_(TRIG_B_OUTPUT).1, LED10.anode
  N23: R6.Pin_1, J10_(TRIG_C_OUTPUT).1, LED11.anode
  N24: R7.Pin_1, J11_(TRIG_D_OUTPUT).1, LED12.anode
  N25: R8.Pin_1, J12_(TRIG_E_OUTPUT).1, LED13.anode
  N26: R9.Pin_1, J13_(TRIG_F_OUTPUT).1, LED14.anode

notes:
  02 ONEBANG, Shelfisizer Module #2: 6-Channel Hysteresis Trigger -rld, 0.1b

custom parts:
  Adafruit Metro Mini: We sure love the ATmega328 here at Adafruit, and we use them a lot for our own projects. The processor has plenty of GPIO, Analog inputs, hardware UART SPI and I2C, timers and PWM galore - just enough for most simple projects. When we need to go small, we use a Pro Trinket 3V or 5V, but if you want to have USB-to-Serial built in, we reach for an Adafruit METRO Mini. METRO Mini is the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
