# Fritzing sketch 03_DUSTDIRT (saved by Fritzing 0.9.3b)
breadboards: 1

parts:
  Part1 = Adafruit Metro Mini [part_number="Adafruit #2590"]
  GND = BANANA_CONN [package=banana_conn]
  +5V = BANANA_CONN [package=banana_conn]
  R1 = Resistor [tolerance=±5% resistance=100k package=THT]
  R2 = Resistor [tolerance=±5% resistance=100k package=THT]
  R3 = Resistor [tolerance=±5% resistance=100k package=THT]
  R4 = Resistor [tolerance=±5% resistance=100k package=THT]
  R5 = Resistor [tolerance=±5% resistance=100k package=THT]
  R6 = Resistor [tolerance=±5% resistance=100k package=THT]
  J1_(B2_TRIG_INPUT) = BANANA_CONN [package=banana_conn]
  J2_(H2_TRIG_INPUT) = BANANA_CONN [package=banana_conn]
  J3_(L2_TRIG_INPUT) = BANANA_CONN [package=banana_conn]
  J4_(B1_TRIG_INPUT) = BANANA_CONN [package=banana_conn]
  J5_(H1_TRIG_INPUT) = BANANA_CONN [package=banana_conn]
  J6_(L1_TRIG_INPUT) = BANANA_CONN [package=banana_conn]
  U1 = 74HC4051 [package=so16]
  R8_(H1_Param_INPUT) = Rotary Potentiometer (Large) [maximum_resistance=10kΩ package=THT]
  R9_(B1_Param_INPUT) = Rotary Potentiometer (Large) [maximum_resistance=10kΩ package=THT]
  R10_(L2_Param_INPUT) = Rotary Potentiometer (Large) [maximum_resistance=10kΩ package=THT]
  R11_(H2_Param_INPUT) = Rotary Potentiometer (Large) [maximum_resistance=10kΩ package=THT]
  R12_(B2_Param_INPUT) = Rotary Potentiometer (Large) [maximum_resistance=10kΩ package=THT]
  R13_(LFO_Rate_INPUT) = Rotary Potentiometer (Large) [maximum_resistance=10kΩ package=THT]
  R14_(LFO_Depth_INPUT) = Rotary Potentiometer (Large) [maximum_resistance=10kΩ package=THT]
  R7_(L1_Param_INPUT) = Rotary Potentiometer (Large) [maximum_resistance=10kΩ package=THT]
  R15 = Resistor [tolerance=±5% resistance=68 package=THT]
  C2 = Electrolytic Capacitor [capacitance=1µF package="100 mil [THT, electrolytic]"]
  R16 = Resistor [tolerance=±5% resistance=60 package=THT]
  C3 = Electrolytic Capacitor [capacitance=10µF package="100 mil [THT, electrolytic]"]
  R17 = Resistor [tolerance=±5% resistance=51 package=THT]
  R18 = Resistor [tolerance=±5% resistance=68 package=THT]
  C4 = Electrolytic Capacitor [capacitance=10µF package="100 mil [THT, electrolytic]"]
  J7_(L1_OUTPUT) = BANANA_CONN [package=banana_conn]
  J8_(H1_OUTPUT) = BANANA_CONN [package=banana_conn]
  J9_(B1_OUTPUT) = BANANA_CONN [package=banana_conn]
  C1 = Electrolytic Capacitor [capacitance=0.47µF package="100 mil [THT, electrolytic]"]
  R19 = Resistor [tolerance=±5% resistance=51 package=THT]
  C5 = Electrolytic Capacitor [capacitance=220µF package="100 mil [THT, electrolytic]"]
  C6 = Electrolytic Capacitor [capacitance=330µF package="100 mil [THT, electrolytic]"]
  R20 = Resistor [tolerance=±5% resistance=1 package=THT]
  C7 = Electrolytic Capacitor [capacitance=1µF package="100 mil [THT, electrolytic]"]
  R21 = Resistor [tolerance=±5% resistance=51 package=THT]
  R22 = Resistor [tolerance=±5% resistance=68 package=THT]
  C8 = Electrolytic Capacitor [capacitance=0.47µF package="100 mil [THT, electrolytic]"]
  J10_(L2_OUTPUT) = BANANA_CONN [package=banana_conn]
  J11_(H2_OUTPUT) = BANANA_CONN [package=banana_conn]
  J12_(B2_OUTPUT) = BANANA_CONN [package=banana_conn]
  S1_(Mode_Toggle_INPUT) = Toggle Switch [package=THT]

nets:
  N1: Part1.AD5/SCL, U1.C
  N2: Part1.AD4/SDA, U1.B
  N3: Part1.AD3, U1.A
  N4: Part1.AD2, S1_(Mode_Toggle_INPUT).L1
  N5: Part1.AD1, R1.Pin_1, J1_(B2_TRIG_INPUT).1
  N6: Part1.AD0, U1.IO
  N7: Part1.IO12, R2.Pin_1, J2_(H2_TRIG_INPUT).1
  N8: Part1.IO11, C7.+
  N9: Part1.IO10, C6.+
  N10: Part1.IO9, R19.Pin_0
  N11: Part1.IO8, R3.Pin_1, J3_(L2_TRIG_INPUT).1
  N12: Part1.IO7, R4.Pin_1, J4_(B1_TRIG_INPUT).1
  N13: Part1.IO6, C3.+
  N14: Part1.IO5, C2.+
  N15: Part1.IO4, R5.Pin_1, J5_(H1_TRIG_INPUT).1
  N16: Part1.IO3, R15.Pin_0
  N17: Part1.IO2, R6.Pin_1, J6_(L1_TRIG_INPUT).1
  +5V: Part1.+5V, U1.VDD, R8_(H1_Param_INPUT).leg1, R9_(B1_Param_INPUT).leg1, R10_(L2_Param_INPUT).leg1, R11_(H2_Param_INPUT).leg1, R12_(B2_Param_INPUT).leg1, R13_(LFO_Rate_INPUT).leg1, R14_(LFO_Depth_INPUT).leg1, R7_(L1_Param_INPUT).leg1
  GND: Part1.GND, GND.1, R1.Pin_0, R2.Pin_0, R3.Pin_0, R4.Pin_0, R5.Pin_0, R6.Pin_0, U1.INH, U1.VEE, U1.VSS, R8_(H1_Param_INPUT).leg2, R9_(B1_Param_INPUT).leg2, R10_(L2_Param_INPUT).leg2, R11_(H2_Param_INPUT).leg2, R12_(B2_Param_INPUT).leg2, R13_(LFO_Rate_INPUT).leg2, R14_(LFO_Depth_INPUT).leg2, R7_(L1_Param_INPUT).leg2, R16.Pin_1, R17.Pin_1, C4.-, C1.-, C5.-, R20.Pin_1, R21.Pin_1, C8.-, S1_(Mode_Toggle_INPUT).COM
  N18: Part1.VIN, +5V.1
  N19: U1.IO4, R11_(H2_Param_INPUT).wiper
  N20: U1.IO6, R13_(LFO_Rate_INPUT).wiper
  N21: U1.IO7, R14_(LFO_Depth_INPUT).wiper
  N22: U1.IO5, R12_(B2_Param_INPUT).wiper
  N23: U1.IO3, R10_(L2_Param_INPUT).wiper
  N24: U1.IO0, R7_(L1_Param_INPUT).wiper
  N25: U1.IO1, R8_(H1_Param_INPUT).wiper
  N26: U1.IO2, R9_(B1_Param_INPUT).wiper
  N27: R15.Pin_1, J7_(L1_OUTPUT).1, C1.+
  N28: C2.-, R16.Pin_0, J8_(H1_OUTPUT).1
  N29: C3.-, R17.Pin_0, R18.Pin_0, J9_(B1_OUTPUT).1
  N30: R18.Pin_1, C4.+
  N31: R19.Pin_1, C5.+, J10_(L2_OUTPUT).1
  N32: C6.-, R20.Pin_0, J11_(H2_OUTPUT).1
  N33: C7.-, R21.Pin_0, R22.Pin_0, J12_(B2_OUTPUT).1
  N34: R22.Pin_1, C8.+

notes:
  03 DUSTDIRT, Shelfisizer Module #3: Low Fidelity Drum/Noise Source -rld, 0.1b

custom parts:
  Adafruit Metro Mini: We sure love the ATmega328 here at Adafruit, and we use them a lot for our own projects. The processor has plenty of GPIO, Analog inputs, hardware UART SPI and I2C, timers and PWM galore - just enough for most simple projects. When we need to go small, we use a Pro Trinket 3V or 5V, but if you want to have USB-to-Serial built in, we reach for an Adafruit METRO Mini. METRO Mini is the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
