# Fritzing sketch 04_LOOKUP (saved by Fritzing 0.9.3b)
breadboards: 2

parts:
  Part1 = Adafruit Metro Mini [part_number="Adafruit #2590"]
  GND = BANANA_CONN [package=banana_conn]
  +5V = BANANA_CONN [package=banana_conn]
  Part3 = Analog Digital MUX Breakout
  Part4 = Analog Digital MUX Breakout
  Part5 = Analog Digital MUX Breakout
  U1 = 74HC595 [package="DIP16 [THT]"]
  U2 = 74HC595 [package="DIP16 [THT]"]
  R1 = Resistor [tolerance=±5% resistance=220 package=THT]
  R2 = Resistor [tolerance=±5% resistance=220 package=THT]
  R3 = Resistor [tolerance=±5% resistance=220 package=THT]
  R4 = Resistor [tolerance=±5% resistance=220 package=THT]
  R5 = Resistor [tolerance=±5% resistance=220 package=THT]
  R6 = Resistor [tolerance=±5% resistance=220 package=THT]
  R7 = Resistor [tolerance=±5% resistance=220 package=THT]
  R8 = Resistor [tolerance=±5% resistance=220 package=THT]
  R9 = Resistor [tolerance=±5% resistance=220 package=THT]
  R10 = Resistor [tolerance=±5% resistance=220 package=THT]
  R11 = Resistor [tolerance=±5% resistance=220 package=THT]
  R12 = Resistor [tolerance=±5% resistance=220 package=THT]
  LED1 = LED - 5mm [color="Green (570nm)" package="5 mm [THT]"]
  LED2 = LED - 5mm [color="Blue (430nm)" package="5 mm [THT]"]
  LED3 = LED - 5mm [color="Green (570nm)" package="5 mm [THT]"]
  LED4 = LED - 5mm [color="Blue (430nm)" package="5 mm [THT]"]
  LED5 = LED - 5mm [color="Blue (430nm)" package="5 mm [THT]"]
  LED6 = LED - 5mm [color="Green (570nm)" package="5 mm [THT]"]
  LED7 = LED - 5mm [color="Blue (430nm)" package="5 mm [THT]"]
  LED8 = LED - 5mm [color="Green (570nm)" package="5 mm [THT]"]
  LED9 = LED - 5mm [color="Green (570nm)" package="5 mm [THT]"]
  LED10 = LED - 5mm [color="Blue (430nm)" package="5 mm [THT]"]
  LED11 = LED - 5mm [color="Green (570nm)" package="5 mm [THT]"]
  LED12 = LED - 5mm [color="Blue (430nm)" package="5 mm [THT]"]
  R13 = Resistor [tolerance=±5% resistance=100k package=THT]
  R14 = Resistor [tolerance=±5% resistance=100k package=THT]
  R15 = Resistor [tolerance=±5% resistance=100k package=THT]
  J1_(A_INPUT) = BANANA_CONN [package=banana_conn]
  J2_(B_INPUT) = BANANA_CONN [package=banana_conn]
  J3_(C_INPUT) = BANANA_CONN [package=banana_conn]
  J4_(A_OUTPUT) = BANANA_CONN [package=banana_conn]
  J5_(B_OUTPUT) = BANANA_CONN [package=banana_conn]
  J6_(C_OUTPUT) = BANANA_CONN [package=banana_conn]
  R16 = Rotary Potentiometer (Large) [maximum_resistance=10kΩ package=THT]
  R17 = Rotary Potentiometer (Large) [maximum_resistance=10kΩ package=THT]
  R18 = Rotary Potentiometer (Large) [maximum_resistance=10kΩ package=THT]
  R19 = Rotary Potentiometer (Large) [maximum_resistance=10kΩ package=THT]
  R20 = Rotary Potentiometer (Large) [maximum_resistance=10kΩ package=THT]
  R21 = Rotary Potentiometer (Large) [maximum_resistance=10kΩ package=THT]
  R22 = Rotary Potentiometer (Large) [maximum_resistance=10kΩ package=THT]
  R23 = Rotary Potentiometer (Large) [maximum_resistance=10kΩ package=THT]
  R24 = Rotary Potentiometer (Large) [maximum_resistance=10kΩ package=THT]
  R25 = Rotary Potentiometer (Large) [maximum_resistance=10kΩ package=THT]
  R26 = Rotary Potentiometer (Large) [maximum_resistance=10kΩ package=THT]
  R27 = Rotary Potentiometer (Large) [maximum_resistance=10kΩ package=THT]
  R28 = Rotary Potentiometer (Large) [maximum_resistance=10kΩ package=THT]
  R29 = Rotary Potentiometer (Large) [maximum_resistance=10kΩ package=THT]
  R30 = Rotary Potentiometer (Large) [maximum_resistance=10kΩ package=THT]
  R31 = Rotary Potentiometer (Large) [maximum_resistance=10kΩ package=THT]
  S1_(Mode_1_INPUT) = Toggle Switch [package=THT]
  S2_(Mode_2_INPUT) = Toggle Switch [package=THT]

nets:
  N1: Part1.AD5/SCL, U1.SH_CP, U2.SH_CP
  N2: Part1.AD4/SDA, U1.ST_CP, U2.ST_CP
  N3: Part1.AD3, U1.DS
  N4: Part1.AD2, R15.Pin_0, J3_(C_INPUT).1
  N5: Part1.AD1, R14.Pin_0, J2_(B_INPUT).1
  N6: Part1.AD0, R13.Pin_0, J1_(A_INPUT).1
  N7: Part1.IO13, Part3.S3
  N8: Part1.IO12, Part3.S2
  N9: Part1.IO11, Part3.S1
  N10: Part1.IO10, Part3.S0
  N11: Part1.IO9, Part4.S3
  N12: Part1.IO8, Part4.S2
  N13: Part1.IO7, Part4.S1
  N14: Part1.IO6, Part4.S0
  N15: Part1.IO5, Part5.S3
  N16: Part1.IO4, Part5.S2
  N17: Part1.IO3, Part5.S1
  N18: Part1.IO2, Part5.S0
  N19: Part1.IO1, S2_(Mode_2_INPUT).L1
  N20: Part1.IO0, S1_(Mode_1_INPUT).L1
  VCC: Part1.+5V, Part3.VCC, Part4.VCC, Part5.VCC, U1.MR, U1.VCC, U2.MR, U2.VCC, R16.leg1, R17.leg1, R18.leg1, R19.leg1, R20.leg1, R21.leg1, R22.leg1, R23.leg1, R24.leg1, R25.leg1, R26.leg1, R27.leg1, R28.leg1, R29.leg1, R30.leg1, R31.leg1
  GND: Part1.GND, GND.1, Part3.GND, Part3.EN, Part4.GND, Part4.EN, Part5.GND, Part5.EN, U1.GND, U1.OE, U2.Q4, U2.Q5, U2.Q6, U2.Q7, U2.GND, U2.Q7', U2.OE, LED1.cathode, LED2.cathode, LED3.cathode, LED4.cathode, LED5.cathode, LED6.cathode, LED7.cathode, LED8.cathode, LED9.cathode, LED10.cathode, LED11.cathode, LED12.cathode, R13.Pin_1, R14.Pin_1, R15.Pin_1, R16.leg2, R17.leg2, R18.leg2, R19.leg2, R20.leg2, R21.leg2, R22.leg2, R23.leg2, R24.leg2, R25.leg2, R26.leg2, R27.leg2, R28.leg2, R29.leg2, R30.leg2, R31.leg2, S1_(Mode_1_INPUT).COM, S2_(Mode_2_INPUT).COM
  N21: Part1.VIN, +5V.1
  N22: Part3.C0, Part4.C0, Part5.C0, R16.wiper
  N23: Part3.C1, Part4.C1, Part5.C1, R17.wiper
  N24: Part3.C2, Part4.C2, Part5.C2, R18.wiper
  N25: Part3.C3, Part4.C3, Part5.C3, R19.wiper
  N26: Part3.C4, Part4.C4, Part5.C4, R20.wiper
  N27: Part3.C5, Part4.C5, Part5.C5, R21.wiper
  N28: Part3.C6, Part4.C6, Part5.C6, R22.wiper
  N29: Part3.C7, Part4.C7, Part5.C7, R23.wiper
  N30: Part3.C8, Part4.C8, Part5.C8, R24.wiper
  N31: Part3.C9, Part4.C9, Part5.C9, R25.wiper
  N32: Part3.C10, Part4.C10, Part5.C10, R26.wiper
  N33: Part3.C11, Part4.C11, Part5.C11, R27.wiper
  N34: Part3.C12, Part4.C12, Part5.C12, R28.wiper
  N35: Part3.C13, Part4.C13, Part5.C13, R29.wiper
  N36: Part3.C14, Part4.C14, Part5.C14, R30.wiper
  N37: Part3.C15, Part4.C15, Part5.C15, R31.wiper
  N38: Part3.SIG, J6_(C_OUTPUT).1
  N39: Part4.SIG, J5_(B_OUTPUT).1
  N40: Part5.SIG, J4_(A_OUTPUT).1
  N41: U1.Q1, R2.Pin_1
  N42: U1.Q2, R3.Pin_1
  N43: U1.Q3, R4.Pin_1
  N44: U1.Q4, R5.Pin_1
  N45: U1.Q5, R6.Pin_1
  N46: U1.Q6, R7.Pin_1
  N47: U1.Q7, R8.Pin_1
  N48: U1.Q7', U2.DS
  N49: U1.Q0, R1.Pin_1
  N50: U2.Q1, R10.Pin_1
  N51: U2.Q2, R11.Pin_1
  N52: U2.Q3, R12.Pin_1
  N53: U2.Q0, R9.Pin_1
  N54: R1.Pin_0, LED1.anode
  N55: R2.Pin_0, LED2.anode
  N56: R3.Pin_0, LED3.anode
  N57: R4.Pin_0, LED4.anode
  N58: R5.Pin_0, LED5.anode
  N59: R6.Pin_0, LED6.anode
  N60: R7.Pin_0, LED7.anode
  N61: R8.Pin_0, LED8.anode
  N62: R9.Pin_0, LED9.anode
  N63: R10.Pin_0, LED10.anode
  N64: R11.Pin_0, LED11.anode
  N65: R12.Pin_0, LED12.anode

notes:
  04 LOOKUP, Shelfisizer Module #4: 16-stage Voltage-Indexed Sequencer -rld, 0.1b

custom parts:
  Adafruit Metro Mini: We sure love the ATmega328 here at Adafruit, and we use them a lot for our own projects. The processor has plenty of GPIO, Analog inputs, hardware UART SPI and I2C, timers and PWM galore - just enough for most simple projects. When we need to go small, we use a Pro Trinket 3V or 5V, but if you want to have USB-to-Serial built in, we reach for an Adafruit METRO Mini. METRO Mini is the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
