# Fritzing sketch 05_SQUARE (saved by Fritzing 0.9.3b)
breadboards: 1

parts:
  GND = BANANA_CONN [package=banana_conn]
  +5V = BANANA_CONN [package=banana_conn]
  U1 = LM393 [package=so08]
  U2 = LM393 [package=so08]
  U3 = LM393 [package=so08]
  R2 = Resistor [tolerance=±5% resistance=330 package=THT]
  R1 = Resistor [tolerance=±5% resistance=330 package=THT]
  R3 = Resistor [tolerance=±5% resistance=330 package=THT]
  R5 = Resistor [tolerance=±5% resistance=330 package=THT]
  R4 = Resistor [tolerance=±5% resistance=330 package=THT]
  R6 = Resistor [tolerance=±5% resistance=330 package=THT]
  R7 = Resistor [tolerance=±5% resistance=100k package=THT]
  R8 = Resistor [tolerance=±5% resistance=100k package=THT]
  R9 = Resistor [tolerance=±5% resistance=100k package=THT]
  R10 = Resistor [tolerance=±5% resistance=100k package=THT]
  R11 = Resistor [tolerance=±5% resistance=100k package=THT]
  R12 = Resistor [tolerance=±5% resistance=100k package=THT]
  J1_(A_INPUT) = BANANA_CONN [package=banana_conn]
  J2_(B_INPUT) = BANANA_CONN [package=banana_conn]
  J3_(C_INPUT) = BANANA_CONN [package=banana_conn]
  J4_(D_INPUT) = BANANA_CONN [package=banana_conn]
  J5_(E_INPUT) = BANANA_CONN [package=banana_conn]
  J6_(F_INPUT) = BANANA_CONN [package=banana_conn]
  J7_(A_OUTPUT) = BANANA_CONN [package=banana_conn]
  J8_(B_OUTPUT) = BANANA_CONN [package=banana_conn]
  J9_(C_OUTPUT) = BANANA_CONN [package=banana_conn]
  J10_(D_OUTPUT) = BANANA_CONN [package=banana_conn]
  J11_(E_OUTPUT) = BANANA_CONN [package=banana_conn]
  J12_(F_OUTPUT) = BANANA_CONN [package=banana_conn]

nets:
  N1: GND.1, U1.G1_-IN, U1.G1_V-, U1.G2_-IN, U2.G1_-IN, U2.G1_V-, U2.G2_-IN, U3.G1_-IN, U3.G1_V-, U3.G2_-IN, R7.Pin_0, R8.Pin_0, R9.Pin_0, R10.Pin_0, R11.Pin_0, R12.Pin_0
  N2: +5V.1, U1.G1_V+, U2.G1_V+, U3.G1_V+, R2.Pin_0, R1.Pin_0, R3.Pin_0, R5.Pin_0, R4.Pin_0, R6.Pin_0
  N3: U1.G1_OUT, R1.Pin_1, J7_(A_OUTPUT).1
  N4: U1.G1_+IN, R7.Pin_1, J1_(A_INPUT).1
  N5: U1.G2_+IN, R8.Pin_1, J2_(B_INPUT).1
  N6: U1.G2_OUT, R2.Pin_1, J8_(B_OUTPUT).1
  N7: U2.G1_OUT, R3.Pin_1, J9_(C_OUTPUT).1
  N8: U2.G1_+IN, R9.Pin_1, J3_(C_INPUT).1
  N9: U2.G2_+IN, R10.Pin_1, J4_(D_INPUT).1
  N10: U2.G2_OUT, R4.Pin_1, J10_(D_OUTPUT).1
  N11: U3.G1_OUT, R5.Pin_1, J11_(E_OUTPUT).1
  N12: U3.G1_+IN, R11.Pin_1, J5_(E_INPUT).1
  N13: U3.G2_+IN, R12.Pin_1, J6_(F_INPUT).1
  N14: U3.G2_OUT, R6.Pin_1, J12_(F_OUTPUT).1

notes:
  05 SQUARE, 6-channel Square Up Comparator -rld, 0.1b
