# Fritzing sketch 06_SHIFT (saved by Fritzing 0.9.3b)
breadboards: 1

parts:
  Part1 = Adafruit Metro Mini [part_number="Adafruit #2590"]
  GND = BANANA_CONN [package=banana_conn]
  +9V = BANANA_CONN [package=banana_conn]
  C1 = Tantalum Capacitor [capacitance=0.1µF package="100 mil [THT, tantalum]"]
  C2 = Tantalum Capacitor [capacitance=0.1µF package="100 mil [THT, tantalum]"]
  C3 = Tantalum Capacitor [capacitance=0.1µF package="100 mil [THT, tantalum]"]
  C4 = Tantalum Capacitor [capacitance=0.1µF package="100 mil [THT, tantalum]"]
  C5 = Tantalum Capacitor [capacitance=0.1µF package="100 mil [THT, tantalum]"]
  C6 = Tantalum Capacitor [capacitance=0.1µF package="100 mil [THT, tantalum]"]
  C7 = Tantalum Capacitor [capacitance=0.1µF package="100 mil [THT, tantalum]"]
  C8 = Tantalum Capacitor [capacitance=0.1µF package="100 mil [THT, tantalum]"]
  C9 = Ceramic Capacitor [capacitance=0.01µF package="100 mil [THT, multilayer]"]
  C10 = Ceramic Capacitor [capacitance=0.01µF package="100 mil [THT, multilayer]"]
  C11 = Ceramic Capacitor [capacitance=0.01µF package="100 mil [THT, multilayer]"]
  C12 = Ceramic Capacitor [capacitance=0.01µF package="100 mil [THT, multilayer]"]
  C13 = Ceramic Capacitor [capacitance=0.01µF package="100 mil [THT, multilayer]"]
  C14 = Ceramic Capacitor [capacitance=0.01µF package="100 mil [THT, multilayer]"]
  C15 = Ceramic Capacitor [capacitance=0.01µF package="100 mil [THT, multilayer]"]
  C16 = Ceramic Capacitor [capacitance=0.01µF package="100 mil [THT, multilayer]"]
  C18 = Ceramic Capacitor [capacitance=0.01µF package="100 mil [THT, multilayer]"]
  C19 = Ceramic Capacitor [capacitance=0.01µF package="100 mil [THT, multilayer]"]
  C20 = Ceramic Capacitor [capacitance=0.01µF package="100 mil [THT, multilayer]"]
  C21 = Ceramic Capacitor [capacitance=0.01µF package="100 mil [THT, multilayer]"]
  C22 = Ceramic Capacitor [capacitance=0.01µF package="100 mil [THT, multilayer]"]
  C23 = Ceramic Capacitor [capacitance=0.01µF package="100 mil [THT, multilayer]"]
  J1_(INPUT_L) = BANANA_CONN [package=banana_conn]
  J2_(L_1_OUTPUT) = BANANA_CONN [package=banana_conn]
  J3_(L_2_OUTPUT) = BANANA_CONN [package=banana_conn]
  J4_(L_3_OUTPUT) = BANANA_CONN [package=banana_conn]
  J5_(L_4_OUTPUT) = BANANA_CONN [package=banana_conn]
  J6_(INPUT_R) = BANANA_CONN [package=banana_conn]
  J7_(R_1_OUTPUT) = BANANA_CONN [package=banana_conn]
  J8_(R_2_OUTPUT) = BANANA_CONN [package=banana_conn]
  J9_(R_3_OUTPUT) = BANANA_CONN [package=banana_conn]
  J10_(R_4_OUTPUT) = BANANA_CONN [package=banana_conn]
  C24 = Ceramic Capacitor [capacitance=0.01µF package="100 mil [THT, multilayer]"]
  IC1 = IC, DIP package, 8 pins [chip_label=LF398]
  IC2 = IC, DIP package, 8 pins [chip_label=LF398]
  IC4 = IC, DIP package, 8 pins [chip_label=LF398]
  IC7 = IC, DIP package, 8 pins [chip_label=LF398]
  IC8 = IC, DIP package, 8 pins [chip_label=LF398]
  IC5 = IC, DIP package, 8 pins [chip_label=LF398]
  IC3 = IC, DIP package, 8 pins [chip_label=LF398]
  IC6 = IC, DIP package, 8 pins [chip_label=LF398]
  C17 = Ceramic Capacitor [capacitance=0.01µF package="100 mil [THT, multilayer]"]
  J11_(L_END_OUTPUT) = BANANA_CONN [package=banana_conn]
  J12_(R_END_OUTPUT) = BANANA_CONN [package=banana_conn]
  J13_(TRIGGER_L_INPUT) = BANANA_CONN [package=banana_conn]
  J14_(TRIGGER_R_INPUT) = BANANA_CONN [package=banana_conn]
  R13 = Resistor [tolerance=±5% resistance=100k package=THT]
  R14 = Resistor [tolerance=±5% resistance=100k package=THT]
  S1_(Manual_L_INPUT) = Round Pushbutton
  S2_(Manual_R_INPUT) = Round Pushbutton

nets:
  N1: Part1.AD5/SCL, S2_(Manual_R_INPUT).leg0
  N2: Part1.AD4/SDA, S1_(Manual_L_INPUT).leg0
  N3: Part1.AD3, J14_(TRIGGER_R_INPUT).1, R14.Pin_0
  N4: Part1.AD2, J13_(TRIGGER_L_INPUT).1, R13.Pin_0
  N5: Part1.IO11, J12_(R_END_OUTPUT).1
  N6: Part1.IO10, IC8.pin8
  N7: Part1.IO9, IC7.pin8
  N8: Part1.IO8, IC6.pin8
  N9: Part1.IO7, IC5.pin8
  N10: Part1.IO6, J11_(L_END_OUTPUT).1
  N11: Part1.IO5, IC4.pin8
  N12: Part1.IO4, IC3.pin8
  N13: Part1.IO3, IC2.pin8
  N14: Part1.IO2, IC1.pin8
  N15: Part1.GND, GND.1, C1.-, C2.-, C3.-, C4.-, C5.-, C6.-, C7.-, C8.-, C9.0, C10.0, C11.0, C12.0, C13.0, C14.0, C15.0, C16.0, C18.0, C18.1, C19.0, C19.1, C20.0, C20.1, C21.0, C21.1, C22.0, C22.1, C23.0, C23.1, C24.0, C24.1, IC1.pin4, IC1.pin7, IC2.pin4, IC2.pin7, IC4.pin4, IC4.pin7, IC7.pin4, IC7.pin7, IC8.pin4, IC8.pin7, IC5.pin4, IC5.pin7, IC3.pin4, IC3.pin7, IC6.pin4, IC6.pin7, C17.0, C17.1, R13.Pin_1, R14.Pin_1, S1_(Manual_L_INPUT).leg1, S2_(Manual_R_INPUT).leg1
  N16: Part1.VIN, +9V.1, C9.1, C10.1, C11.1, C12.1, C13.1, C14.1, C15.1, C16.1, IC1.pin1, IC1.pin2, IC2.pin1, IC2.pin2, IC4.pin1, IC4.pin2, IC7.pin1, IC7.pin2, IC8.pin1, IC8.pin2, IC5.pin1, IC5.pin2, IC3.pin1, IC3.pin2, IC6.pin1, IC6.pin2
  N17: C1.+, IC1.pin6
  N18: C2.+, IC2.pin6
  N19: C3.+, IC3.pin6
  N20: C4.+, IC4.pin6
  N21: C5.+, IC5.pin6
  N22: C6.+, IC6.pin6
  N23: C7.+, IC7.pin6
  N24: C8.+, IC8.pin6
  N25: J1_(INPUT_L).1, IC1.pin3
  N26: J2_(L_1_OUTPUT).1, IC1.pin5, IC2.pin3
  N27: J3_(L_2_OUTPUT).1, IC2.pin5, IC3.pin3
  N28: J4_(L_3_OUTPUT).1, IC4.pin3, IC3.pin5
  N29: J5_(L_4_OUTPUT).1, IC4.pin5
  N30: J6_(INPUT_R).1, IC5.pin3
  N31: J7_(R_1_OUTPUT).1, IC5.pin5, IC6.pin3
  N32: J8_(R_2_OUTPUT).1, IC7.pin3, IC6.pin5
  N33: J9_(R_3_OUTPUT).1, IC7.pin5, IC8.pin3
  N34: J10_(R_4_OUTPUT).1, IC8.pin5

notes:
  06 SHIFT, Shelfisizer Module #6: Dual 4-Stage Analog Shift Register -rld, 0.1b

custom parts:
  Adafruit Metro Mini: We sure love the ATmega328 here at Adafruit, and we use them a lot for our own projects. The processor has plenty of GPIO, Analog inputs, hardware UART SPI and I2C, timers and PWM galore - just enough for most simple projects. When we need to go small, we use a Pro Trinket 3V or 5V, but if you want to have USB-to-Serial built in, we reach for an Adafruit METRO Mini. METRO Mini is the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
