# Fritzing sketch 08_QUANT (saved by Fritzing 0.9.4)
breadboards: 1

parts:
  Part1 = Adafruit Metro Mini [part_number="Adafruit #2590"]
  J1_(Ext_Pulse_INPUT) = BANANA_CONN [package=banana_conn]
  R1 = Resistor [tolerance=±5% resistance=100k package=THT]
  LED14 = LED - 5mm [color="Red (633nm)" package="5 mm [THT]"]
  Part3 = Adafruit MCP4725 Breakout Board - 12-Bit DAC [part_number="Adafruit #935"]
  Part4 = Adafruit MCP4725 Breakout Board - 12-Bit DAC [part_number="Adafruit #935"]
  R10 = Resistor [tolerance=±5% resistance=100k package=THT]
  J1_(Ext_Pulse_INPUT)1 = BANANA_CONN [package=banana_conn]
  J1_(Ext_Pulse_INPUT)2 = BANANA_CONN [package=banana_conn]
  J1_(Ext_Pulse_INPUT)3 = BANANA_CONN [package=banana_conn]
  J1_(Ext_Pulse_INPUT)4 = BANANA_CONN [package=banana_conn]
  R7_(L1_Param_INPUT)1 = Rotary Potentiometer (Large) [maximum_resistance=10kΩ package=THT]
  R7_(L1_Param_INPUT)2 = Rotary Potentiometer (Large) [maximum_resistance=10kΩ package=THT]
  R13 = Resistor [tolerance=±5% resistance=100k package=THT]
  R14 = Resistor [tolerance=±5% resistance=100k package=THT]
  J1_(Ext_Pulse_INPUT)5 = BANANA_CONN [package=banana_conn]
  S2_(Mode_2_INPUT)1 = Toggle Switch [package=THT]
  S2_(Mode_2_INPUT)2 = Toggle Switch [package=THT]
  S2_(Mode_2_INPUT)3 = Toggle Switch [package=THT]
  S2_(Mode_2_INPUT)4 = Toggle Switch [package=THT]
  S2_(Mode_2_INPUT)5 = Toggle Switch [package=THT]
  LED15 = LED - 5mm [color="Red (633nm)" package="5 mm [THT]"]
  LED16 = LED - 5mm [color="Red (633nm)" package="5 mm [THT]"]
  LED17 = LED - 5mm [color="Red (633nm)" package="5 mm [THT]"]
  LED18 = LED - 5mm [color="Red (633nm)" package="5 mm [THT]"]
  S2_(Mode_2_INPUT)6 = Toggle Switch [package=THT]
  S2_(Mode_2_INPUT)7 = Toggle Switch [package=THT]

nets:
  N1: Part1.AD5/SCL, Part3.SCL, Part4.SCL
  N2: Part1.AD4/SDA, Part3.SDA, Part4.SDA
  N3: Part1.AD3, R7_(L1_Param_INPUT)2.wiper
  N4: Part1.AD2, R7_(L1_Param_INPUT)1.wiper
  N5: Part1.AD1, R10.Pin_0, J1_(Ext_Pulse_INPUT)4.1
  N6: Part1.AD0, R1.Pin_0, J1_(Ext_Pulse_INPUT)3.1
  N7: Part1.IO10, S2_(Mode_2_INPUT)7.L1
  N8: Part1.IO9, S2_(Mode_2_INPUT)6.L1
  N9: Part1.IO8, S2_(Mode_2_INPUT)5.L1
  N10: Part1.IO7, S2_(Mode_2_INPUT)4.L1
  N11: Part1.IO6, S2_(Mode_2_INPUT)3.L1
  N12: Part1.IO5, S2_(Mode_2_INPUT)2.L1
  N13: Part1.IO4, S2_(Mode_2_INPUT)1.L1
  N14: Part1.IO3, J1_(Ext_Pulse_INPUT).1, R14.Pin_1
  N15: Part1.IO2, R13.Pin_1, J1_(Ext_Pulse_INPUT)5.1
  VDD: Part1.+5V, Part3.VDD, Part4.VDD, Part4.A0, R7_(L1_Param_INPUT)1.leg1, R7_(L1_Param_INPUT)2.leg1
  GND: Part1.GND, R1.Pin_1, LED14.cathode, Part3.GND, Part4.GND, R10.Pin_1, R7_(L1_Param_INPUT)1.leg2, R7_(L1_Param_INPUT)2.leg2, R13.Pin_0, R14.Pin_0, LED15.cathode, LED16.cathode, LED17.cathode, LED18.cathode, S2_(Mode_2_INPUT)6.COM, S2_(Mode_2_INPUT)7.COM
  N16: LED14.anode, S2_(Mode_2_INPUT)1.COM
  N17: Part3.VOUT, J1_(Ext_Pulse_INPUT)1.1
  N18: Part4.VOUT, J1_(Ext_Pulse_INPUT)2.1
  N19: S2_(Mode_2_INPUT)2.COM, LED15.anode
  N20: S2_(Mode_2_INPUT)3.COM, LED16.anode
  N21: S2_(Mode_2_INPUT)4.COM, LED17.anode
  N22: S2_(Mode_2_INPUT)5.COM, LED18.anode

notes:
  02 ONEBANG, Shelfisizer Module #2: 6-Channel Hysteresis Trigger -rld, 0.1b

custom parts:
  Adafruit Metro Mini: We sure love the ATmega328 here at Adafruit, and we use them a lot for our own projects. The processor has plenty of GPIO, Analog inputs, hardware UART SPI and I2C, timers and PWM galore - just enough for most simple projects. When we need to go small, we use a Pro Trinket 3V or 5V, but if you want to have USB-to-Serial built in, we reach for an Adafruit METRO Mini. METRO Mini is the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
  Adafruit MCP4725 Breakout Board - 12-Bit DAC: Your microcontroller probably has an ADC (analog -> digital converter) but does it have a DAC (digital -> analog converter)??? Now it can! This breakout board features the easy-to-use MCP4725 12-bit DAC. Control it via I2C and send it the value you want it to output, and the VOUT pin will have it. Great for audio / analog projects, such as when you can't use PWM but need a sine wave or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
