# Fritzing sketch 09_ENVY (saved by Fritzing 0.9.4)
breadboards: 1

parts:
  Part1 = Adafruit Metro Mini [part_number="Adafruit #2590"]
  J1_(Ext_Pulse_INPUT) = BANANA_CONN [package=banana_conn]
  Part3 = Adafruit MCP4725 Breakout Board - 12-Bit DAC [part_number="Adafruit #935"]
  Part4 = Adafruit MCP4725 Breakout Board - 12-Bit DAC [part_number="Adafruit #935"]
  J1_(Env_1_OUTPUT) = BANANA_CONN [package=banana_conn]
  J2_(Env_2_OUTPUT) = BANANA_CONN [package=banana_conn]
  R7_(L1_Param_INPUT)1 = Rotary Potentiometer (Large) [maximum_resistance=10kΩ package=THT]
  R7_(L1_Param_INPUT)2 = Rotary Potentiometer (Large) [maximum_resistance=10kΩ package=THT]
  R13 = Resistor [tolerance=±5% resistance=100k package=THT]
  R14 = Resistor [tolerance=±5% resistance=100k package=THT]
  J1_(Ext_Pulse_INPUT)5 = BANANA_CONN [package=banana_conn]
  S2_(Mode_2_INPUT)6 = Toggle Switch [package=THT]  # not connected
  Part5 = Adafruit ADS1015 12Bit I2C ADC [part_number="Adafruit #1083"]
  Part6 = Adafruit ADS1015 12Bit I2C ADC [part_number="Adafruit #1083"]
  R15 = Resistor [tolerance=±5% resistance=100k package=THT]
  R16 = Resistor [tolerance=±5% resistance=100k package=THT]
  J1_(Ext_Pulse_INPUT)6 = BANANA_CONN [package=banana_conn]
  J1_(Ext_Pulse_INPUT)7 = BANANA_CONN [package=banana_conn]
  J1_(Ext_Pulse_INPUT)8 = BANANA_CONN [package=banana_conn]
  J1_(Ext_Pulse_INPUT)9 = BANANA_CONN [package=banana_conn]
  R17 = Resistor [tolerance=±5% resistance=220 package=THT]
  R18 = Resistor [tolerance=±5% resistance=220 package=THT]
  LED6 = LED - 5mm [color="Red (633nm)" package="5 mm [THT]"]
  LED7 = LED - 5mm [color="Red (633nm)" package="5 mm [THT]"]
  R19 = Resistor [tolerance=±5% resistance=220 package=THT]
  R20 = Resistor [tolerance=±5% resistance=220 package=THT]

nets:
  N1: Part1.AD5/SCL, Part3.SCL, Part4.SCL, Part5.SCL, Part6.SCL
  N2: Part1.AD4/SDA, Part3.SDA, Part4.SDA, Part5.SDA, Part6.SDA
  N3: Part1.IO10, R20.Pin_1
  N4: Part1.IO9, R19.Pin_1
  N5: Part1.IO7, R17.Pin_0
  N6: Part1.IO6, R18.Pin_0
  N7: Part1.IO5, R16.Pin_1, J1_(Ext_Pulse_INPUT)7.1
  N8: Part1.IO4, R15.Pin_1, J1_(Ext_Pulse_INPUT)6.1
  N9: Part1.IO3, J1_(Ext_Pulse_INPUT).1, R14.Pin_1
  N10: Part1.IO2, R13.Pin_1, J1_(Ext_Pulse_INPUT)5.1
  VDD: Part1.+5V, Part3.VDD, Part4.VDD, Part4.A0, R7_(L1_Param_INPUT)1.leg1, R7_(L1_Param_INPUT)2.leg1, Part5.VDD, Part6.ADDR, Part6.VDD
  GND: Part1.GND, Part3.GND, Part4.GND, R7_(L1_Param_INPUT)1.leg2, R7_(L1_Param_INPUT)2.leg2, R13.Pin_0, R14.Pin_0, Part5.ADDR, Part5.GND, Part6.GND, R15.Pin_0, R16.Pin_0, LED6.cathode, LED7.cathode
  N11: Part3.VOUT, J1_(Env_1_OUTPUT).1
  N12: Part4.VOUT, J2_(Env_2_OUTPUT).1
  N13: J1_(Ext_Pulse_INPUT)8.1, R18.Pin_1
  N14: J1_(Ext_Pulse_INPUT)9.1, R17.Pin_1
  N15: LED6.anode, R19.Pin_0
  N16: LED7.anode, R20.Pin_0

notes:
  02 ONEBANG, Shelfisizer Module #2: 6-Channel Hysteresis Trigger -rld, 0.1b

custom parts:
  Adafruit Metro Mini: We sure love the ATmega328 here at Adafruit, and we use them a lot for our own projects. The processor has plenty of GPIO, Analog inputs, hardware UART SPI and I2C, timers and PWM galore - just enough for most simple projects. When we need to go small, we use a Pro Trinket 3V or 5V, but if you want to have USB-to-Serial built in, we reach for an Adafruit METRO Mini. METRO Mini is the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
  Adafruit MCP4725 Breakout Board - 12-Bit DAC: Your microcontroller probably has an ADC (analog -> digital converter) but does it have a DAC (digital -> analog converter)??? Now it can! This breakout board features the easy-to-use MCP4725 12-bit DAC. Control it via I2C and send it the value you want it to output, and the VOUT pin will have it. Great for audio / analog projects, such as when you can't use PWM but need a sine wave or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
  Adafruit ADS1015 12Bit I2C ADC: For microcontrollers without an analog-to-digital converter or when you want a higher-precision ADC, the ADS1015 provides 12-bit precision at 3300 samples/second over I2C. The chip can be configured as 4 single-ended input channels, or two differential channels. As a nice bonus, it even includes a programmable gain amplifier, up to x16, to help boost up smaller single/differential signals to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
